# Fritzing sketch Aquifer_V_1_0 (saved by Fritzing 0.9.2b)
breadboards: 2

parts:
  Part1 = Arduino Uno (Rev3)  # not connected
  Part2 = Arduino Uno (Rev3)  # not connected
  K1 = Relay [part_number=FRS1B-S package=THT]  # not connected
  K2 = Relay [part_number=FRS1B-S package=THT]  # not connected
  K3 = Relay [part_number=FRS1B-S package=THT]  # not connected
  K4 = Relay [part_number=FRS1B-S package=THT]  # not connected
  DHT1 = DHT22 Humidity and Temperature Sensor  # not connected
  S1 = Pushbutton [package=THT]
  S2 = Pushbutton [package=THT]
  S3 = Pushbutton [package=THT]
  S4 = Pushbutton [package=THT]
  S5 = Pushbutton [package=THT]
  Part3 = Arduino Board Ethernet
  DS3 = DS18B20 1-Wire Temperature Sensor Probe Cable
  DS4 = DS18B20 1-Wire Temperature Sensor Probe Cable
  Part4 = Arduino Board Ethernet
  DAC1 = MCP4725 12-bit DAC Breakout  # not connected

nets:
  N1: S1.leg0, S2.leg0, S3.leg0, S4.leg0, S5.leg0
  N2: S1.leg1, S2.leg1, S3.leg1, S4.leg1, S5.leg1, Part3.D2_PWM, Part3.D3_PWM, Part3.D5_PWM, Part3.D6_PWM, Part3.D7
  VDD: DS3.VDD, DS4.VDD
  N3: DS3.shield, Part4.D9_PWM
  N4: DS4.shield, Part4.D8

custom parts:
  MCP4725 12-bit DAC Breakout: MCP4725 12-bit Digital-to-Analog Converter
